# Fritzing sketch tricorderCircuit (saved by Fritzing 0.8.5b)
circuit board: 8.46667cm x 5.64444cm
breadboards: 1

parts:
  Part1 = Arduino Uno (Rev3)
  LCD1 = LCD screen
  R1 = Rotary Potentiometer (Small) [maximum_resistance=100kΩ package=THT]
  R2 = Resistor [tolerance=±5% resistance=220 package=THT]
  LED1 = LED - 5mm [color="Yellow (585nm)" package="5 mm [THT]"]
  LED2 = LED - 5mm [color="Green (565nm)" package="5 mm [THT]"]
  LED3 = LED - 5mm [color="Green (565nm)" package="5 mm [THT]"]
  R3 = Resistor [tolerance=±5% resistance=220 package=THT]
  R4 = Resistor [tolerance=±5% resistance=220 package=THT]
  R5 = Resistor [tolerance=±5% resistance=220 package=THT]
  R6 = Photocell (LDR) [package=THT]
  R7 = Resistor [tolerance=±5% resistance=10k package=THT]
  T1 = LM35 Temperature Sensor [package="TO92 [THT]"]
  VCC1 = Battery block 9V

nets:
  N1: Part1.A0, T1.Vout
  N2: Part1.A1, R6.pin_1, R7.Pin_1
  N3: Part1.D8, LED1.anode
  N4: Part1.D9_PWM, LED2.anode
  N5: Part1.D11_PWM/MOSI, LCD1.E
  N6: Part1.D12/MISO, LCD1.RS
  N7: Part1.D13/SCK, LED3.anode
  GND: Part1.GND, LCD1.VSS, LCD1.R/W, LCD1.LED-, R1.leg2, R3.Pin_0, R4.Pin_0, R5.Pin_0, T1.GND, VCC1.-
  N8: Part1.D2, LCD1.DB7
  N9: Part1.D3_PWM, LCD1.DB6
  N10: Part1.D4, LCD1.DB5
  N11: Part1.D5_PWM, LCD1.DB4
  5V: Part1.5V, LCD1.VDD, R1.leg1, R2.Pin_0, R6.pin_0, R7.Pin_0, T1.+Vs
  N12: Part1.VIN, VCC1.+
  N13: LCD1.V0, R1.wiper
  N14: LCD1.LED+, R2.Pin_1
  N15: LED1.cathode, R3.Pin_1
  N16: LED2.cathode, R4.Pin_1
  N17: LED3.cathode, R5.Pin_1
